// Logisim project alovt.circ as structural Verilog: 1 circuit, main circuit main
module main (
  input  [7:0] Data_In,
  input  CLK,
  input  EN,
  output [7:0] Data_Out
);

  wire [7:0] d_ff_1_p1;

  // D_Flip_Flop d_ff_1: pin names not known; wires that end beside it: d_ff_1_p1[0], CLK, CLK, EN, Data_Out[2]
  // D_Flip_Flop d_ff_2: pin names not known; wires that end beside it: CLK, d_ff_1_p1[1], CLK, CLK, EN, Data_Out[6]
  // D_Flip_Flop d_ff_3: pin names not known; wires that end beside it: CLK, d_ff_1_p1[2], CLK, CLK, Data_Out[2]
  // D_Flip_Flop d_ff_4: pin names not known; wires that end beside it: CLK, d_ff_1_p1[3], CLK, CLK, Data_Out[3]
  // D_Flip_Flop d_ff_5: pin names not known; wires that end beside it: CLK, d_ff_1_p1[4], CLK, CLK, Data_Out[4]
  // D_Flip_Flop d_ff_6: pin names not known; wires that end beside it: CLK, d_ff_1_p1[5], CLK, CLK, Data_Out[5]
  // D_Flip_Flop d_ff_7: pin names not known; wires that end beside it: CLK, d_ff_1_p1[6], CLK, CLK, EN, Data_Out[6]
  // D_Flip_Flop d_ff_8: pin names not known; wires that end beside it: CLK, d_ff_1_p1[7], CLK, EN, Data_Out[7]

  assign Data_Out[1:0] = {Data_Out[6], Data_Out[2]};
endmodule
